# Fritzing sketch PostCycla (saved by Fritzing 0.9.3b)
stripboards: 1

parts:
  Nano1 = Arduino Nano v2.3
  J1 = female pin header, 10 pins [form="♀ (female)"]
  J2 = female pin header, 10 pins [form="♀ (female)"]
  R1 = Resistor [tolerance=±5% resistance=220 package=THT]
  R2 = Resistor [tolerance=±5% resistance=10k package=THT]
  J3 = Basic Servo
  CNY1 = CNY70

nets:
  GND: Nano1.GND, J2.pin9, R1.Pin_0, R2.Pin_1, J3.gnd
  N1: Nano1.D3, J1.pin10, J3.pulse
  N2: Nano1.D12, J1.pin1, R2.Pin_0, CNY1.Emisor
  VIN: Nano1.VIN, J2.pin10, J3.vcc, CNY1.Colector, CNY1.Anodo
  N3: R1.Pin_1, CNY1.Catodo

custom parts:
  CNY70: Sensor de Infrarojos de corto alcance.
